# Fritzing sketch schematic (saved by Fritzing 1.0.2b)

parts:
  Componente1 = Arduino Nano (Rev3.0) (ICSP)
  LCD2 = LCD screen
  LCM1602_IIC1 = LCM1602 IIC [part_number="LCM1602 IIC" chip_label="LCM1602 IIC" package="DIP (Dual Inline) [THT]"]
  HLK-PM1 = HLK-PM01
  S5 = Round Pushbutton [mn=PINAVVIO]
  S6 = Round Pushbutton [mn=PINDURATA]
  S7 = Round Pushbutton
  S8 = Round Pushbutton [mn=RESET]
  KY-1 = Keyes Relay [package=THT]

nets:
  N1: Componente1.D12/MISO, S5.leg0
  GND: Componente1.GND, LCM1602_IIC1.GND, HLK-PM1.-Vo, S5.leg1, S6.leg1, S7.leg1, S8.leg1, KY-1.ground
  N2: Componente1.RESET, S8.leg0
  5V: Componente1.5V, LCM1602_IIC1.VCC, HLK-PM1.+Vo, KY-1.power
  N3: Componente1.A5, LCM1602_IIC1.SCL
  N4: Componente1.A4, LCM1602_IIC1.SDA
  N5: Componente1.A2, S7.leg0
  N6: Componente1.A1, S6.leg0
  N7: Componente1.A0, KY-1.signal
  VSS: LCD2.VSS, LCM1602_IIC1.VSS
  VDD: LCD2.VDD, LCM1602_IIC1.VDD
  N8: LCD2.V0, LCM1602_IIC1.V0
  N9: LCD2.RS, LCM1602_IIC1.RS
  N10: LCD2.R/W, LCM1602_IIC1.RW
  N11: LCD2.E, LCM1602_IIC1.E
  N12: LCD2.DB0, LCM1602_IIC1.D0
  N13: LCD2.DB1, LCM1602_IIC1.D1
  N14: LCD2.DB2, LCM1602_IIC1.D2
  N15: LCD2.DB3, LCM1602_IIC1.D3
  N16: LCD2.DB4, LCM1602_IIC1.D4
  N17: LCD2.DB5, LCM1602_IIC1.D5
  N18: LCD2.DB6, LCM1602_IIC1.D6
  N19: LCD2.DB7, LCM1602_IIC1.D7
  N20: LCD2.LED+, LCM1602_IIC1.A
  N21: LCD2.LED-, LCM1602_IIC1.K
  N22: LCM1602_IIC1.LED_A, LCM1602_IIC1.LED_B

custom parts:
  LCM1602 IIC: I2C-Module to use a 1602 or 2004 LCD on with the wire.h libory Serial LCD Modul
  Keyes Relay: The Keyes 5V relay module is suitable for SCM development, home appliance control. It uses a 5V~12V TIL control signal which can control DC / AC signal.
